# Fritzing sketch Arduino-ACS712 (saved by Fritzing 0.9.3b)
breadboards: 1

parts:
  Placa_Arduino_Uno = Arduino Uno (Rev3)
  Sensor_ACS712 = ACS712 Low Current Sensor Board v12

nets:
  N1: Placa_Arduino_Uno.A0, Sensor_ACS712.VO
  GND: Placa_Arduino_Uno.GND, Sensor_ACS712.GND
  5V: Placa_Arduino_Uno.5V, Sensor_ACS712.5V
