# Fritzing sketch ESP32-ACS712 (saved by Fritzing 0.9.3b)
breadboards: 1

parts:
  Simplified = DOIT Esp32 DevKit v1 (30 pins long, 11 pins width) [part_number=ESP32S-PIN30]
  Componente1 = ACS712 Low Current Sensor Board v12
  R1 = Resistor [tolerance=±5% resistance=220 package="2010 [SMD]"]
  R2 = Resistor [tolerance=±5% resistance=220 package="2010 [SMD]"]
  R3 = Resistor [tolerance=±5% resistance=220 package="0402 [SMD]"]
  KY-1 = Keyes Relay [package=THT]

nets:
  N1: Simplified.3V3, KY-1.power
  GND: Simplified.GND, Componente1.GND, R3.Pin_1, KY-1.ground
  N2: Simplified.D19, KY-1.signal
  N3: Simplified.D34, R1.Pin_1, R2.Pin_0
  VIN: Simplified.VIN, Componente1.5V
  N4: Componente1.IP+, KY-1.NC, KY-1.C, KY-1.NO
  N5: Componente1.VO, R1.Pin_0
  N6: R2.Pin_1, R3.Pin_0

custom parts:
  DOIT Esp32 DevKit v1 (30 pins long, 11 pins width): The DOIT Esp32 DevKit v1 is one of the development board created by DOIT to evaluate the ESP-WROOM-32 module. It is based on the ESP32 microcontroller that boasts Wifi, Bluetooth, Ethernet and Low Power support all in a single chip. (vanepp) made breadboard work, adjusted pin numbering and labels and reduced size of schematic and cleaned up pcb. This chip is 30pins long (2 x15) and 11 pins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
  Keyes Relay: The Keyes 5V relay module is suitable for SCM development, home appliance control. It uses a 5V~12V TIL control signal which can control DC / AC signal.
